// Logisim project d8_new.circ as structural Verilog: 37 circuits, main circuit main
module main (
  input  in_1,
  input  [2:0] R,
  input  [2:0] W,
  input  in_4,
  input  in_5
);

  wire ic_xx02_1_y1, ic_xx02_1_y3, ic_xx02_1_y4, pipeline_1_skip, undriven_2, undriven_3, undriven_4,
       undriven_5, undriven_6, undriven_7, undriven_8, undriven_9, undriven_10, undriven_11;
  wire [2:0] undriven_14, undriven_15;
  wire [7:0] rom_1_data, undriven, undriven_12, undriven_13;
  wire [15:0] address_unit_1_a, address_unit_2_a, constant_register_1_q;

  IC_xx02 ic_xx02_1 (
    .Y1(ic_xx02_1_y1), .A1(in_1), .B1(in_1), .Y4(ic_xx02_1_y4), .B4(ic_xx02_1_y1), .A4(pipeline_1_skip),
    .Y3(ic_xx02_1_y3), .B3(ic_xx02_1_y4), .A3(ic_xx02_1_y4));  // open: Y2, A2, B2
  pipeline pipeline_1 (
    .CLK(in_1), .D(undriven), .SKIP(pipeline_1_skip));  // open: LOAD_M, FLAGS, CYCLE, CTRL0, CTRL1, CTRL2, CTRL3
  Pull_Resistor pull_resistor_1 (.node(ic_xx02_1_y4));
  constant_register constant_register_1 (
    .D(rom_1_data), .LOAD_CONST_LOW(in_5), .LOAD_CONST_HIGH(1'b0), .CLK(ic_xx02_1_y4),
    .Q(constant_register_1_q));
  address_unit address_unit_1 (
    .A(address_unit_1_a), .LOAD_TL(1'b0), .LOAD_TH(1'b0), .W_N(W), .R_N(R), .CLK(ic_xx02_1_y4),
    .PC_CE_L(in_4), .SP_U_DL(1'b1), .SP_CE_L(1'b1), .RA_CE_L(1'b1), .SI_U_DL(1'b1), .SI_CE_L(1'b1),
    .DI_U_DL(1'b1), .DI_CE_L(1'b1), .const16(constant_register_1_q), .nCLK(ic_xx02_1_y3));  // open: D
  ROM #(.addrWidth(16)) rom_1 (.addr(address_unit_1_a), .data(rom_1_data));  // open: sel
  address_unit address_unit_2 (
    .A(address_unit_2_a), .LOAD_TL(undriven_3), .LOAD_TH(undriven_2), .W_N(undriven_15), .R_N(undriven_14),
    .D(undriven_12), .PC_CE_L(undriven_4), .SP_U_DL(undriven_5), .SP_CE_L(undriven_6), .RA_CE_L(undriven_7),
    .SI_U_DL(undriven_8), .SI_CE_L(undriven_9), .DI_U_DL(undriven_10), .DI_CE_L(undriven_11));  // open: CLK, const16, nCLK
  gpr_unit gpr_unit_1 (.data(undriven_13));  // open: Q, CLK, W_N, GPR_WE_L, U_DL, CE_L, LOAD_L, R_N, GPR_OE_L

  // Notes on the sheet:
  //   CLK#
  //   CLK
  //   contents of rom_1 (hex, n*v repeats v):
  //   c5 18 93 bf 27 2f ef 1a 46 35 d1 2a 5f c6 64 8e 55 21 8 76 a5 f1 12 56 df e5 4a b0 83 86 9f e8 1c 53
  //   a 4d a6 74 ab 94 77 69 76 27 61 c7 9f 4a d1 7d de 9e 6b 56 56 44 d4 ac 8d 8d 2 bf fe 5b dd dd a1 c2
  //   9f d8 82 f9 a3 d3 88 f8 84 73 1c 4b 5e ed b0 e7 3f c9 76 b1 ed df fd ae 7d db 32 3b 4f 69 14 73 c4 6
  //   1e 40 3a ae 53 18 9b 4c f3 64 d5 c9 73 ba 54 e9 6b 9 17 c4 21 dd 9e 62 e3 22 62 17 ca 7a 8f 4a 51 1
  //   7f 2 ac cc fd b7 f8 26 8d fd 18 aa 2e e9 80 64 eb 91 ab df f0 82 b3 ab a4 2b c6 c4 be 35 fd 33 cb 87
  //   a3 c0 92 4b 81 5 33 51 d6 20 ab ea da f7 bf c0 43 ae f9 20 91 b3 24 e0 21 4f 93 1 2c 89 5f 8c 5c 30
  //   a5 1 0 25 79 f9 b 9 bd 16 9c f0 c3 8a 45 c2 a3 64 83 e1 d1 66 d9 27 4c 5d 4f 91 dc 2d 37 86 42 2d 77
  //   2e 5a 5d c 30 f3 e3 32 24 e0 bb eb 4 e5 e3 9d fc 7d 4d a5 70 8c fd ff 4b 92 23 3 c c4 f7 35 46 2d 87
  //   61 33 1c aa 4d b2 7 9a da e2 2 52 75 d1 5f 36 45 13 5d 1b 6e 3b 6d bf 79 ed 51 17 b b6 c3 3f 80 cf
  //   5b 77 76 f3 5b 3e d3 f8 72 20 9b cf 82 ce c ab 34 8f cc ec bc b4 a3 66 8b 9f ab d4 d0 79 a8 d6 ae 11
  //   1f 89 b9 4e fb ab e9 dc e8 9d af fa 7e de 61 26 f5 fe a5 2b ba 8 bc 66 2 7 45 f5 1b bd 9 ee 98 cd 95
  //   8f 93 47 2e 14 c2 f6 5e 6 6c 96 f0 29 48 66 c1 4f 1b 1d 4b 3 ba 79 e8 21 e1 fe cb e8 3b 6a 42 1d 26
  //   83 1f a4 7e a3 ac 8f 36 87 23 4 c0 af 46 3f 7a 74 4d 63 f5 29 5a 6b 4d 83 f5 46 6a e5 80 5d 34 68 70
  //   6e d5 f3 a5 fb dc b3 e1 3b e3 1f 9f 9a 71 eb d4 6a 3b ab a6 9a c0 f7 81 d4 bd ec 5d 61 f6 5 e1 2f 9c
  //   97 87 c9 1e 67 c8 19 32 a1 7d 27 32 11 b1 71 1e 12 70 33 72 bf f9 80 d1 26 a2 a5 f5 99 46 f5 41 81
  //   be 5e da 85 bd a0 b3 f 55 45 4c 52 d4 5c 96 ac 25 35 4d a1 ca 22 16 5c 73 43 97 f6 c0 f9 27 ef 14 86
  //   c8 5d 31 f1 68 da b3 80 98 22 db 36 1 c d4 6e dd 98 84 6d 92 91 e8 2b 99 f2 2d dd fd e0 39 31 f 42
  //   29 f8 5d 12 c7 d3 ae da 5 49 d1 c5 43 d9 33 db 7c 91 f5 10 fa ac 30 e6 a8 79 8c 95 3b e6 d5 ea a5 e8
  //   57 f4 bf f4 81 a 62 61 bf 9b 5f 28 37 f 21 d0 7e 9b 76 95 67 13 32 91 9 3c 4 a6 53 73 7 19 1d 6c 39
  //   3a 2f 3b 87 1 75 32 7f cf 57 ca 70 e9 3c 45 13 94 b 86 52 6e 17 b3 9c 1a 3a 6a 54 9 46 cd 6a 5b c1
  //   3c 6b a8 c5 19 da 71 c9 24 ba 20 73 53 f0 c8 75 16 f1 66 3d 8a 7b 8a 77 5d bd 26 31 7d 63 b7 5c 1f
  //   88 1f 11 37 42 50 84 a4 ef 9e a4 18 4b 2e 60 e7 1e c8 56 fa cb 3b 63 46 a7 5a e4 3d 21 74 25 15 6e d
  //   58 ce 83 66 a7 95 b3 71 d8 81 2 e8 b9 ff 77 7a 65 1 76 a7 da db 57 d4 cf aa ef ac 6d b6 fa 31 95 49
  //   ee 21 e9 19 e5 93 81 4a fe 9 39 43 8a e8 74 8a 86 db 59 15 a8 d1 42 69 e2 c7 a1 d7 d1 ab 5e 94 aa a6
  //   47 33 fe d8 a2 65 81 53 e 5 62 49 5e 96 39 6f 80 a9 72 57 c7 99 46 6a 16 77 6f d8 da f3 f1 9b ae 37
  //   2c 2 f7 eb 90 90 9d 98 22 74 50 3e 8 a3 84 db f0 11 47 a4 e8 aa 79 c5 ea 2 50 f7 30 af 26 de 7a 5e
  //   20 2f 8e 5f ce 8d 80 32 64 af b8 dd ef da 5f 30 26 3 db 77 35 a4 5c bf 9f c8 b4 eb de 2d 48 83 f 6b
  //   85 78 47 bb 43 b9 25 82 c7 87 64 32 ec db b7 81 b3 7d 53 6e e6 3f f8 62 16 da e1 70 a7 ad 9d 24 48
  //   16 31 74 6c 2 56 1e 2b 3e 9 6f 7b c7 c 48 ae aa ab 39 12 8b 20 7f 20 39 4f ed 7d 8d bf cb e6 96 e7
  //   1b 67 99 ee a2 29 50 a4 b3 6b 2b 9 56 ad 9 2e f6 a5 7f 6b 46 23 db 91 ab 76 f9 5e 6e c0 c1 9b 1b f0
  //   61 e6 ec 2b 17 57 7a 63 ec 72 68 4d 16 2b a6 b6 d2 3 a3 de 1c 80 34 7e 90 a c2 83 a8 a9 59 cb 84 29
  //   e8 a8 2b b0 e5 fd f1 9a f0 b9 ff ae f5 7f a6 90 9b af 77 d2 5a 62 8f 8e 1b 39 e3 2d 31 2a b5 8a eb
  //   b9 3b 6b 1f 7c 65 b4 89 15 a2 c9 5f 8f ab a9 2f 41 93 12 d0 f 22 6c e 91 d0 ef f7 26 e8 90 59 d1 f1
  //   5f e0 50 2a ef 65 c1 7e d0 24 7a ca 48 e3 6a 31 aa f0 67 f 57 5e 8e 3e c9 32 a0 79 96 e0 3b a4 61 76
  //   80 1e 59 f4 f0 d0 f8 35 a7 e2 72 ba 32 57 ba ef d6 77 2d 8d a4 1a 95 52 c2 f2 f4 79 ff 3c bc e2 9e
  //   bf b6 a1 4a dc fa 60 ca a0 af e4 69 76 76 df 58 d4 e3 41 2b 0 38 c6 46 ae a2 28 58 22 1a 2 f1 2e 64
  //   b8 72 ca a3 f 23 29 21 0 63 36 b1 c4 d4 38 1b 69 c3 67 c7 bb ac f7 bd 5f 10 fb fa 9b 2a 6f 5f fa 38
  //   71 db a1 b7 3e af a2 e3 61 6d b8 2f db 35 8 bf 5d b7 e3 33 6d 6a f1 2a 45 eb 55 da bf d2 d c4 22 bd
  //   d f5 b5 ff cb 58 c3 fa 72 2b b2 6e a1 8b d3 51 d1 d5 cf eb 2 d 87 8d 66 e8 a8 76 81 6c ae 69 a3 56
  //   e6 32 be 22 9a fe 20 c5 bc fa ca 13 bd ac 35 5b 78 44 a2 f 9d f6 8e 77 44 8 25 f1 8d 1e 9d a0 e3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
endmodule

module address_unit (
  input  [2:0] W_N,
  input  [2:0] R_N,
  input  CLK,
  input  nCLK,
  input  LOAD_TL,
  input  LOAD_TH,
  input  [7:0] D,
  input  PC_CE_L,
  input  SP_U_DL,
  input  SP_CE_L,
  input  RA_CE_L,
  input  SI_U_DL,
  input  SI_CE_L,
  input  DI_U_DL,
  input  DI_CE_L,
  input  [15:0] const16,
  output [15:0] A
);

  wire ic_xx02_1_y1, ic_xx02_1_y2, ic_xx02_1_y4, ic_xx04_1_y2, ic_xx04_1_y5, READ_y1_l, READ_y2_l, READ_y3_l,
       READ_y4_l, READ_y5_l, READ_y6_l, READ_y7_l, WRITE_y1_l, WRITE_y2_l, WRITE_y3_l, WRITE_y4_l,
       WRITE_y5_l, WRITE_y7_l;
  wire [7:0] th_q, tl_q;
  wire [15:0] di_out_8, il_reg16_1_out_8, pc_out_8, si_out_8, sp_out_8;

  IC_xx04 ic_xx04_1 (
    .A2(LOAD_TL), .A5(LOAD_TH), .Y2(ic_xx04_1_y2), .Y5(ic_xx04_1_y5));  // open: A1, A3, A4, A6, Y1, Y3, Y4, Y6
  IC_xx02 ic_xx02_1 (
    .Y1(ic_xx02_1_y1), .A1(LOAD_TL), .B1(ic_xx02_1_y4), .Y2(ic_xx02_1_y2), .A2(LOAD_TH), .B2(ic_xx02_1_y4),
    .Y4(ic_xx02_1_y4), .B4(WRITE_y7_l), .A4(WRITE_y7_l));  // open: Y3, B3, A3
  IC_xx540 ic_xx540_1 (.OE1_L(ic_xx04_1_y2), .D(D), .OE2_L(1'b0), .Q(A[7:0]));
  IC_xx540 ic_xx540_2 (.OE1_L(ic_xx04_1_y5), .D(D), .OE2_L(1'b0), .Q(A[15:8]));
  IC_xx540 ic_xx540_3 (.OE1_L(1'b0), .D(const16[7:0]), .OE2_L(READ_y6_l), .Q(A[7:0]));
  IC_xx540 ic_xx540_4 (.OE1_L(1'b0), .D(const16[15:8]), .OE2_L(READ_y6_l), .Q(A[15:8]));
  l_reg8 tl (.D(A[7:0]), .CLK(CLK), .LOAD_L(ic_xx02_1_y1), .Q(tl_q));  // open: NC_U_DL, NC_CE2_L, NC_CE1_L, CO_L
  IC_xx540 ic_xx540_5 (.OE1_L(1'b0), .D(tl_q), .OE2_L(READ_y7_l), .Q(A[7:0]));
  IC_xx540 ic_xx540_6 (.OE1_L(1'b0), .D(th_q), .OE2_L(READ_y7_l), .Q(A[15:8]));
  l_reg8 th (.D(A[15:8]), .CLK(CLK), .LOAD_L(ic_xx02_1_y2), .Q(th_q));  // open: NC_U_DL, NC_CE2_L, NC_CE1_L, CO_L
  IC_xx138 WRITE (
    .SEL(W_N), .EN1_L(1'b0), .EN2_L(1'b0), .EN3(CLK), .Y1_L(WRITE_y1_l), .Y2_L(WRITE_y2_l),
    .Y3_L(WRITE_y3_l), .Y4_L(WRITE_y4_l), .Y5_L(WRITE_y5_l), .Y7_L(WRITE_y7_l));  // open: Y0_L, Y6_L
  il_reg16 pc (
    .D(A), .CLK(nCLK), .CE2_L(1'b0), .LOAD_L(WRITE_y1_l), .CE1_L(PC_CE_L), .out_8(pc_out_8));  // open: NC_U_DL, CO_L
  dil_reg16 sp (
    .D(A), .CLK(nCLK), .U_DL(SP_U_DL), .CE2_L(1'b0), .LOAD_L(WRITE_y2_l), .CE1_L(SP_CE_L), .out_8(sp_out_8));  // open: CO_L
  il_reg16 il_reg16_1 (
    .D(A), .CLK(nCLK), .CE2_L(1'b0), .LOAD_L(WRITE_y3_l), .CE1_L(RA_CE_L), .out_8(il_reg16_1_out_8));  // open: NC_U_DL, CO_L
  dil_reg16 si (
    .D(A), .CLK(nCLK), .U_DL(SI_U_DL), .CE2_L(1'b0), .LOAD_L(WRITE_y4_l), .CE1_L(SI_CE_L), .out_8(si_out_8));  // open: CO_L
  dil_reg16 di (
    .D(A), .CLK(nCLK), .U_DL(DI_U_DL), .CE2_L(1'b0), .LOAD_L(WRITE_y5_l), .CE1_L(DI_CE_L), .out_8(di_out_8));  // open: CO_L
  IC_xx574 ic_xx574_1 (.OE_L(1'b0), .D(pc_out_8[7:0]));  // open: O, CP
  IC_xx138 READ (
    .SEL(R_N), .EN1_L(1'b0), .EN2_L(1'b0), .EN3(1'b1), .Y1_L(READ_y1_l), .Y2_L(READ_y2_l), .Y3_L(READ_y3_l),
    .Y4_L(READ_y4_l), .Y5_L(READ_y5_l), .Y6_L(READ_y6_l), .Y7_L(READ_y7_l));  // open: Y0_L
endmodule

module constant_register (
  input  [7:0] D,
  input  LOAD_CONST_LOW,
  input  LOAD_CONST_HIGH,
  input  CLK,
  output [15:0] Q
);

  wire ic_xx08_1_y1, ic_xx08_1_y2;

  IC_xx08 ic_xx08_1 (
    .A1(LOAD_CONST_LOW), .B1(CLK), .Y1(ic_xx08_1_y1), .A2(LOAD_CONST_HIGH), .B2(CLK), .Y2(ic_xx08_1_y2));  // open: A4, B4, Y4, A3, B3, Y3
  IC_xx574 const_low (.OE_L(1'b0), .D(D), .O(Q[7:0]), .CP(ic_xx08_1_y1));
  IC_xx574 const_high (.OE_L(1'b0), .D(D), .O(Q[15:8]), .CP(ic_xx08_1_y2));
endmodule

module ctrl0 (
  input  [1:0] CYCLE,
  input  [15:0] BITS,
  output [7:0] CTRL
);

  ROM #(.addrWidth(18)) rom_1 (.addr({BITS, CYCLE}), .data(CTRL));  // open: sel

  // Notes on the sheet:
  //   SST39SF020A
endmodule

module ctrl1 (
  input  [1:0] CYCLE,
  input  [15:0] BITS,
  output [7:0] CTRL
);

  ROM #(.addrWidth(18)) rom_1 (.addr({BITS, CYCLE}), .data(CTRL));  // open: sel

  // Notes on the sheet:
  //   SST39SF020A
endmodule

module ctrl2 (
  input  [1:0] CYCLE,
  input  [15:0] BITS,
  output [7:0] CTRL
);

  ROM #(.addrWidth(18)) rom_1 (.addr({BITS, CYCLE}), .data(CTRL));  // open: sel

  // Notes on the sheet:
  //   SST39SF020A
endmodule

module ctrl3 (
  input  [1:0] CYCLE,
  input  [15:0] BITS,
  output [7:0] CTRL
);

  ROM #(.addrWidth(18)) rom_1 (.addr({BITS, CYCLE}), .data(CTRL));  // open: sel

  // Notes on the sheet:
  //   SST39SF020A
endmodule

module gpr_unit (
  input  [1:0] W_N,
  input  [1:0] R_N,
  input  GPR_OE_L,
  input  GPR_WE_L,
  input  CLK,
  input  [7:0] data,
  input  U_DL,
  input  CE_L,
  input  LOAD_L,
  output [7:0] Q
);

  wire ic_xx02_1_y1, ic_xx02_1_y2, ic_xx02_1_y4, ic_xx04_1_y3, ic_xx04_1_y4, ic_xx04_1_y5, ic_xx04_1_y6,
       ic_xx139_1_y10_l, ic_xx139_1_y20_l, ic_xx139_1_y21_l, ic_xx139_1_y22_l, ic_xx139_1_y23_l,
       ic_xx139_1_y_11_l, ic_xx139_1_y_12_l, ic_xx139_1_y_13_l;
  wire [7:0] a_q, b_q, c_q, d_q;

  IC_xx02 ic_xx02_1 (
    .Y1(ic_xx02_1_y1), .A1(GPR_WE_L), .B1(ic_xx02_1_y2), .Y2(ic_xx02_1_y2), .A2(CLK), .B2(CLK),
    .Y4(ic_xx02_1_y4), .B4(ic_xx02_1_y1), .A4(ic_xx02_1_y1));  // open: Y3, B3, A3
  IC_xx04 ic_xx04_1 (
    .A3(ic_xx139_1_y_13_l), .A4(ic_xx139_1_y_12_l), .A5(ic_xx139_1_y_11_l), .A6(ic_xx139_1_y10_l),
    .Y3(ic_xx04_1_y3), .Y4(ic_xx04_1_y4), .Y5(ic_xx04_1_y5), .Y6(ic_xx04_1_y6));  // open: A1, A2, Y1, Y2
  dil_reg8 a (
    .D(data), .CLK(ic_xx04_1_y6), .U_DL(U_DL), .CE2_L(CE_L), .LOAD_L(LOAD_L), .CE1_L(1'b0), .Q(a_q));  // open: CO_L
  dil_reg8 b (
    .D(data), .CLK(ic_xx04_1_y5), .U_DL(U_DL), .CE2_L(CE_L), .LOAD_L(LOAD_L), .CE1_L(1'b0), .Q(b_q));  // open: CO_L
  dil_reg8 c (
    .D(data), .CLK(ic_xx04_1_y4), .U_DL(U_DL), .CE2_L(CE_L), .LOAD_L(LOAD_L), .CE1_L(1'b0), .Q(c_q));  // open: CO_L
  dil_reg8 d (
    .D(data), .CLK(ic_xx04_1_y3), .U_DL(U_DL), .CE2_L(CE_L), .LOAD_L(LOAD_L), .CE1_L(1'b0), .Q(d_q));  // open: CO_L
  IC_xx139 ic_xx139_1 (
    .EN_1_L(ic_xx02_1_y4), .SEL_1(W_N), .Y10_L(ic_xx139_1_y10_l), .Y_11_L(ic_xx139_1_y_11_l),
    .Y_12_L(ic_xx139_1_y_12_l), .Y_13_L(ic_xx139_1_y_13_l), .EN_2_L(GPR_OE_L), .SEL_2(R_N),
    .Y20_L(ic_xx139_1_y20_l), .Y21_L(ic_xx139_1_y21_l), .Y22_L(ic_xx139_1_y22_l), .Y23_L(ic_xx139_1_y23_l));
  IC_xx540 ic_xx540_1 (.OE1_L(1'b0), .D(a_q), .OE2_L(ic_xx139_1_y20_l), .Q(Q));
  IC_xx540 ic_xx540_2 (.OE1_L(1'b0), .D(b_q), .OE2_L(ic_xx139_1_y21_l), .Q(Q));
  IC_xx540 ic_xx540_3 (.OE1_L(1'b0), .D(c_q), .OE2_L(ic_xx139_1_y22_l), .Q(Q));
  IC_xx540 ic_xx540_4 (.OE1_L(1'b0), .D(d_q), .OE2_L(ic_xx139_1_y23_l), .Q(Q));
endmodule

module pipeline (
  input  CLK,
  input  [7:0] D,
  input  LOAD_M,
  input  [3:0] FLAGS,
  output SKIP,
  output [1:0] CYCLE,
  output [15:0] CTRL0,
  output [15:0] CTRL1,
  output [15:0] CTRL2,
  output [15:0] CTRL3
);

  wire ic_xx02_1_y1, ic_xx02_1_y2, ic_xx02_1_y4, pull_resistor_1_node;
  wire [3:3] ic_xx163_1_q;
  wire [7:0] ic_xx174_1_q0;
  wire [7:4] ic_xx574_2_o, ic_xx574_4_o, ic_xx574_5_o, ic_xx574_7_o, ic_xx574_8_o, ic_xx574_10_o,
       ic_xx574_11_o, undriven;

  Pull_Resistor #(.pull(1)) pull_resistor_1 (.node(pull_resistor_1_node));
  Transistor #(.\type ("n")) transistor_1 (.in(1'b0), .out(pull_resistor_1_node), .gate(SKIP));
  IC_xx163 ic_xx163_1 (
    .CLR_L(pull_resistor_1_node), .CLK(CLK), .ENP(1'b1), .Q({ic_xx163_1_q[3], SKIP, CYCLE}), .ENT(1'b1),
    .LOAD_L(1'b1));  // open: D, RCO
  IC_xx02 ic_xx02_1 (
    .Y1(ic_xx02_1_y1), .A1(ic_xx02_1_y2), .B1(ic_xx02_1_y2), .Y2(ic_xx02_1_y2), .A2(CYCLE[0]), .B2(CYCLE[1]),
    .Y4(ic_xx02_1_y4), .B4(ic_xx02_1_y1), .A4(SKIP));  // open: Y3, B3, A3
  IC_xx574 ic_xx574_1 (.OE_L(1'b0), .D(D), .O(CTRL0[7:0]), .CP(SKIP));
  IC_xx174 ic_xx174_1 (
    .MR(ic_xx02_1_y4), .D0(D[0]), .D1(D[1]), .D2(D[2]), .D3(D[3]), .Q0(ic_xx174_1_q0[0]),
    .Q1(ic_xx174_1_q0[1]), .Q2(ic_xx174_1_q0[2]), .Q3(ic_xx174_1_q0[3]), .CP(LOAD_M));  // open: D4, D5, Q4, Q5
  IC_xx574 ic_xx574_2 (.OE_L(1'b0), .D({undriven, FLAGS}), .O({ic_xx574_2_o, CTRL0[15:12]}), .CP(SKIP));
  IC_xx574 ic_xx574_3 (.OE_L(1'b0), .D(CTRL0[7:0]), .O(CTRL1[7:0]), .CP(SKIP));
  IC_xx574 ic_xx574_4 (.OE_L(1'b0), .D(ic_xx174_1_q0), .O({ic_xx574_4_o, CTRL1[11:8]}), .CP(SKIP));
  IC_xx574 ic_xx574_5 (.OE_L(1'b0), .D({ic_xx574_2_o, CTRL0[15:12]}), .O({ic_xx574_5_o, CTRL1[15:12]}), .CP(SKIP));
  IC_xx574 ic_xx574_6 (.OE_L(1'b0), .D(CTRL1[7:0]), .O(CTRL2[7:0]), .CP(SKIP));
  IC_xx574 ic_xx574_7 (.OE_L(1'b0), .D({ic_xx574_4_o, CTRL1[11:8]}), .O({ic_xx574_7_o, CTRL2[11:8]}), .CP(SKIP));
  IC_xx574 ic_xx574_8 (.OE_L(1'b0), .D({ic_xx574_5_o, CTRL1[15:12]}), .O({ic_xx574_8_o, CTRL2[15:12]}), .CP(SKIP));
  IC_xx574 ic_xx574_9 (.OE_L(1'b0), .D(CTRL2[7:0]), .O(CTRL3[7:0]), .CP(SKIP));
  IC_xx574 ic_xx574_10 (.OE_L(1'b0), .D({ic_xx574_7_o, CTRL2[11:8]}), .O({ic_xx574_10_o, CTRL3[11:8]}), .CP(SKIP));
  IC_xx574 ic_xx574_11 (.OE_L(1'b0), .D({ic_xx574_8_o, CTRL2[15:12]}), .O({ic_xx574_11_o, CTRL3[15:12]}), .CP(SKIP));

  assign CTRL0[11:8] = 4'b0000;
endmodule

// +-L8
module dil_reg8 (
  input  [7:0] D,
  input  CLK,
  input  U_DL,
  input  CE2_L,
  input  LOAD_L,
  input  CE1_L,
  output CO_L,
  output [7:0] Q
);

  wire ic_xx169_1_rco_l;

  IC_xx169 ic_xx169_1 (
    .U_DL(U_DL), .D(D[3:0]), .ENP_L(CE2_L), .CLK(CLK), .RCO_L(ic_xx169_1_rco_l), .Q(Q[3:0]), .ENT_L(CE1_L),
    .LOAD_L(LOAD_L));
  IC_xx169 ic_xx169_2 (
    .U_DL(U_DL), .D(D[7:4]), .ENP_L(ic_xx169_1_rco_l), .CLK(CLK), .RCO_L(CO_L), .Q(Q[7:4]), .ENT_L(CE1_L),
    .LOAD_L(LOAD_L));
endmodule

// L8
module l_reg8 (
  input  [7:0] D,
  input  CLK,
  input  NC_U_DL,
  input  NC_CE2_L,
  input  LOAD_L,
  input  NC_CE1_L,
  output CO_L,
  output [7:0] Q
);

  wire ic_xx169_1_rco_l;

  IC_xx169 ic_xx169_1 (
    .U_DL(1'b1), .D(D[3:0]), .ENP_L(1'b1), .CLK(CLK), .RCO_L(ic_xx169_1_rco_l), .Q(Q[3:0]), .ENT_L(1'b1),
    .LOAD_L(LOAD_L));
  IC_xx169 ic_xx169_2 (
    .U_DL(1'b1), .D(D[7:4]), .ENP_L(ic_xx169_1_rco_l), .CLK(CLK), .RCO_L(CO_L), .Q(Q[7:4]), .ENT_L(1'b1),
    .LOAD_L(LOAD_L));
endmodule

// +-16
module di_reg16 (
  input  [15:0] D,
  input  CLK,
  input  U_DL,
  input  CE2_L,
  input  NC_LOAD_L,
  input  CE1_L,
  output CO_L,
  output [15:0] out_8
);

  wire ic_xx169_1_rco_l, ic_xx169_2_rco_l, ic_xx169_3_rco_l;

  IC_xx169 ic_xx169_1 (
    .U_DL(U_DL), .D(D[3:0]), .ENP_L(CE2_L), .CLK(CLK), .RCO_L(ic_xx169_1_rco_l), .Q(out_8[3:0]),
    .ENT_L(CE1_L), .LOAD_L(1'b1));
  IC_xx169 ic_xx169_2 (
    .U_DL(U_DL), .D(D[7:4]), .ENP_L(ic_xx169_1_rco_l), .CLK(CLK), .RCO_L(ic_xx169_2_rco_l), .Q(out_8[7:4]),
    .ENT_L(CE1_L), .LOAD_L(1'b1));
  IC_xx169 ic_xx169_3 (
    .U_DL(U_DL), .D(D[11:8]), .ENP_L(ic_xx169_2_rco_l), .CLK(CLK), .RCO_L(ic_xx169_3_rco_l), .Q(out_8[11:8]),
    .ENT_L(CE1_L), .LOAD_L(1'b1));
  IC_xx169 ic_xx169_4 (
    .U_DL(U_DL), .D(D[15:12]), .ENP_L(ic_xx169_3_rco_l), .CLK(CLK), .RCO_L(CO_L), .Q(out_8[15:12]),
    .ENT_L(CE1_L), .LOAD_L(1'b1));
endmodule

// +-L16
module dil_reg16 (
  input  [15:0] D,
  input  CLK,
  input  U_DL,
  input  CE2_L,
  input  LOAD_L,
  input  CE1_L,
  output CO_L,
  output [15:0] out_8
);

  wire ic_xx169_1_rco_l, ic_xx169_2_rco_l, ic_xx169_3_rco_l;

  IC_xx169 ic_xx169_1 (
    .U_DL(U_DL), .D(D[3:0]), .ENP_L(CE2_L), .CLK(CLK), .RCO_L(ic_xx169_1_rco_l), .Q(out_8[3:0]),
    .ENT_L(CE1_L), .LOAD_L(LOAD_L));
  IC_xx169 ic_xx169_2 (
    .U_DL(U_DL), .D(D[7:4]), .ENP_L(ic_xx169_1_rco_l), .CLK(CLK), .RCO_L(ic_xx169_2_rco_l), .Q(out_8[7:4]),
    .ENT_L(CE1_L), .LOAD_L(LOAD_L));
  IC_xx169 ic_xx169_3 (
    .U_DL(U_DL), .D(D[11:8]), .ENP_L(ic_xx169_2_rco_l), .CLK(CLK), .RCO_L(ic_xx169_3_rco_l), .Q(out_8[11:8]),
    .ENT_L(CE1_L), .LOAD_L(LOAD_L));
  IC_xx169 ic_xx169_4 (
    .U_DL(U_DL), .D(D[15:12]), .ENP_L(ic_xx169_3_rco_l), .CLK(CLK), .RCO_L(CO_L), .Q(out_8[15:12]),
    .ENT_L(CE1_L), .LOAD_L(LOAD_L));
endmodule

// +L16
module il_reg16 (
  input  [15:0] D,
  input  CLK,
  input  NC_U_DL,
  input  CE2_L,
  input  LOAD_L,
  input  CE1_L,
  output CO_L,
  output [15:0] out_8
);

  wire ic_xx169_1_rco_l, ic_xx169_2_rco_l, ic_xx169_3_rco_l;

  IC_xx169 ic_xx169_1 (
    .U_DL(1'b1), .D(D[3:0]), .ENP_L(CE2_L), .CLK(CLK), .RCO_L(ic_xx169_1_rco_l), .Q(out_8[3:0]),
    .ENT_L(CE1_L), .LOAD_L(LOAD_L));
  IC_xx169 ic_xx169_2 (
    .U_DL(1'b1), .D(D[7:4]), .ENP_L(ic_xx169_1_rco_l), .CLK(CLK), .RCO_L(ic_xx169_2_rco_l), .Q(out_8[7:4]),
    .ENT_L(CE1_L), .LOAD_L(LOAD_L));
  IC_xx169 ic_xx169_3 (
    .U_DL(1'b1), .D(D[11:8]), .ENP_L(ic_xx169_2_rco_l), .CLK(CLK), .RCO_L(ic_xx169_3_rco_l), .Q(out_8[11:8]),
    .ENT_L(CE1_L), .LOAD_L(LOAD_L));
  IC_xx169 ic_xx169_4 (
    .U_DL(1'b1), .D(D[15:12]), .ENP_L(ic_xx169_3_rco_l), .CLK(CLK), .RCO_L(CO_L), .Q(out_8[15:12]),
    .ENT_L(CE1_L), .LOAD_L(LOAD_L));
endmodule

// L16
module l_reg16 (
  input  [15:0] D,
  input  CLK,
  input  NC_U_DL,
  input  NC_CE2_L,
  input  LOAD_L,
  input  NC_CE1_L,
  output CO_L,
  output [15:0] out_8
);

  wire ic_xx169_1_rco_l, ic_xx169_2_rco_l, ic_xx169_3_rco_l;

  IC_xx169 ic_xx169_1 (
    .U_DL(1'b1), .D(D[3:0]), .ENP_L(1'b1), .CLK(CLK), .RCO_L(ic_xx169_1_rco_l), .Q(out_8[3:0]), .ENT_L(1'b1),
    .LOAD_L(LOAD_L));
  IC_xx169 ic_xx169_2 (
    .U_DL(1'b1), .D(D[7:4]), .ENP_L(ic_xx169_1_rco_l), .CLK(CLK), .RCO_L(ic_xx169_2_rco_l), .Q(out_8[7:4]),
    .ENT_L(1'b1), .LOAD_L(LOAD_L));
  IC_xx169 ic_xx169_3 (
    .U_DL(1'b1), .D(D[11:8]), .ENP_L(ic_xx169_2_rco_l), .CLK(CLK), .RCO_L(ic_xx169_3_rco_l), .Q(out_8[11:8]),
    .ENT_L(1'b1), .LOAD_L(LOAD_L));
  IC_xx169 ic_xx169_4 (
    .U_DL(1'b1), .D(D[15:12]), .ENP_L(ic_xx169_3_rco_l), .CLK(CLK), .RCO_L(CO_L), .Q(out_8[15:12]),
    .ENT_L(1'b1), .LOAD_L(LOAD_L));
endmodule

// xx02
module DIP_xx02 (
  input  Vcc,
  input  A1,
  input  B1,
  input  B4,
  input  A4,
  input  A2,
  input  B2,
  input  B3,
  input  GND,
  input  A3,
  output Y1,
  output Y4,
  output Y2,
  output Y3
);

  nor nor_1 (Y1, A1, B1);
  nor nor_2 (Y2, A2, B2);
  nor nor_3 (Y4, A4, B4);
  nor nor_4 (Y3, A3, B3);

  // Notes on the sheet:
  //   A4: pull=up
  //   B3: pull=up
  //   B4: pull=up
  //   A2: pull=up
  //   Vcc: pull=up
  //   A1: pull=up
  //   B1: pull=up
endmodule

// xx04
module DIP_xx04 (
  input  A1,
  input  Vcc,
  input  A6,
  input  A2,
  input  A5,
  input  A3,
  input  A4,
  input  GND,
  output Y1,
  output Y6,
  output Y2,
  output Y5,
  output Y3,
  output Y4
);

  not not_1 (Y1, A1);
  not not_2 (Y6, A6);
  not not_3 (Y2, A2);
  not not_4 (Y5, A5);
  not not_5 (Y3, A3);
  not not_6 (Y4, A4);

  // Notes on the sheet:
  //   A2: pull=up
  //   A4: pull=up
  //   A6: pull=up
  //   A5: pull=up
  //   Vcc: pull=up
  //   A1: pull=up
  //   A3: pull=up
endmodule

// xx08
module DIP_xx08 (
  input  A1,
  input  Vcc,
  input  B1,
  input  A4,
  input  B4,
  input  A2,
  input  B2,
  input  A3,
  input  B3,
  input  GND,
  output Y1,
  output Y4,
  output Y2,
  output Y3
);

  and and_1 (Y1, B1, A1);
  and and_2 (Y4, A4, B4);
  and and_3 (Y2, B2, A2);
  and and_4 (Y3, A3, B3);
endmodule

module DIP_xx138 (
  input  A,
  input  Vcc,
  input  B,
  input  C,
  input  EN1_L,
  input  EN2_L,
  input  EN3,
  input  GND,
  output Y0_L,
  output Y1_L,
  output Y2_L,
  output Y3_L,
  output Y4_L,
  output Y7_L,
  output Y5_L,
  output Y6_L
);

  wire or_2_out;

  or or_1 (Y7_L, ~C, ~B, ~A, or_2_out);  // OR_Gate
  or or_2 (or_2_out, EN1_L, EN2_L, ~EN3);  // OR_Gate
  or or_3 (Y0_L, C, B, A, or_2_out);
  or or_4 (Y1_L, ~C, B, A, or_2_out);  // OR_Gate
  or or_5 (Y2_L, C, ~B, A, or_2_out);  // OR_Gate
  or or_6 (Y3_L, ~C, ~B, A, or_2_out);  // OR_Gate
  or or_7 (Y4_L, C, B, ~A, or_2_out);  // OR_Gate
  or or_8 (Y5_L, ~C, B, ~A, or_2_out);  // OR_Gate
  or or_9 (Y6_L, C, ~B, ~A, or_2_out);  // OR_Gate

  // Notes on the sheet:
  //   EN1_L: pull=up
  //   A: pull=up
  //   B: pull=up
  //   EN3: pull=up
  //   EN2_L: pull=up
  //   C: pull=up
endmodule

// xx139
module DIP_xx139 (
  input  EN1_L,
  input  Vcc,
  input  A1,
  input  EN2_L,
  input  B1,
  input  A2,
  input  B2,
  input  GND,
  output Y10_L,
  output Y11_L,
  output Y20_L,
  output Y12_L,
  output Y21_L,
  output Y13_L,
  output Y22_L,
  output Y23_L
);

  or or_1 (Y10_L, B1, A1, EN1_L);
  or or_2 (Y11_L, ~B1, A1, EN1_L);  // OR_Gate
  or or_3 (Y12_L, B1, ~A1, EN1_L);  // OR_Gate
  or or_4 (Y13_L, ~B1, ~A1, EN1_L);  // OR_Gate
  or or_5 (Y20_L, B2, A2, EN2_L);
  or or_6 (Y21_L, ~B2, A2, EN2_L);  // OR_Gate
  or or_7 (Y22_L, B2, ~A2, EN2_L);  // OR_Gate
  or or_8 (Y23_L, ~B2, ~A2, EN2_L);  // OR_Gate

  // Notes on the sheet:
  //   B2: pull=up
  //   EN2_L: pull=up
  //   EN1_L: pull=up
  //   A2: pull=up
  //   B1: pull=up
  //   A1: pull=up
endmodule

// xx163
module DIP_xx163 (
  input  CLR_L,
  input  Vcc,
  input  CLK,
  input  A,
  input  B,
  input  C,
  input  D,
  input  ENP,
  input  ENT,
  input  GND,
  input  LOAD_L,
  output RCO,
  output Q_A,
  output Q_B,
  output Q_C,
  output Q_D
);

  wire and_1_out, and_2_out, and_3_out, not_1_out, not_2_out, not_3_out, not_4_out, not_5_out;

  not not_1 (not_1_out, CLR_L);
  and and_1 (and_1_out, ENP, LOAD_L, ENT);
  not not_2 (not_2_out, LOAD_L);
  Counter #(.width(4), .max('hf)) counter_1 (
    .load(not_2_out), .D({D, C, B, A}), .count(and_1_out), .Q({Q_D, Q_C, Q_B, Q_A}), .carry(RCO), .clk(CLK),
    .clr(and_2_out));
  and and_2 (and_2_out, not_1_out, and_3_out);
  and and_3 (and_3_out, not_5_out, CLK);
  not not_3 (not_3_out, CLK);
  not not_4 (not_4_out, not_3_out);
  not not_5 (not_5_out, not_4_out);
endmodule

module DIP_xx169 (
  input  U_DL,
  input  Vcc,
  input  CLK,
  input  A,
  input  B,
  input  C,
  input  D,
  input  ENP_L,
  input  ENT_L,
  input  GND,
  input  LOAD_L,
  output RCO_L,
  output Q_A,
  output Q_B,
  output Q_C,
  output Q_D
);

  wire counter_1_carry, nor_1_out, not_1_out;

  Counter #(.width(4), .max('hf)) counter_1 (
    .load(not_1_out), .D({D, C, B, A}), .count(nor_1_out), .Q({Q_D, Q_C, Q_B, Q_A}), .carry(counter_1_carry),
    .clk(CLK), .clr(1'b0));
  nor nor_1 (nor_1_out, ENP_L, ENT_L);
  not not_1 (not_1_out, LOAD_L);
  not not_2 (RCO_L, counter_1_carry);
endmodule

// xx174
module DIP_xx174 (
  input  MR,
  input  Vcc,
  input  D0,
  input  D5,
  input  D1,
  input  D4,
  input  D2,
  input  D3,
  input  GND,
  input  CP,
  output Q0,
  output Q5,
  output Q1,
  output Q4,
  output Q2,
  output Q3
);

  D_Flip_Flop d_ff_1 (.clk(CP), .D(D0), .Q(Q0), .preset(1'b0), .reset(MR));  // open: Qn, en
  D_Flip_Flop d_ff_2 (.clk(CP), .D(D1), .Q(Q1), .preset(1'b0), .reset(MR));  // open: Qn, en
  D_Flip_Flop d_ff_3 (.clk(CP), .D(D2), .Q(Q2), .preset(1'b0), .reset(MR));  // open: Qn, en
  D_Flip_Flop d_ff_4 (.clk(CP), .D(D5), .Q(Q5), .preset(1'b0), .reset(MR));  // open: Qn, en
  D_Flip_Flop d_ff_5 (.clk(CP), .D(D4), .Q(Q4), .preset(1'b0), .reset(MR));  // open: Qn, en
  D_Flip_Flop d_ff_6 (.clk(CP), .D(D3), .Q(Q3), .preset(1'b0), .reset(MR));  // open: Qn, en
endmodule

// xx193
module DIP_xx193 (
  input  B,
  input  Vcc,
  input  A,
  input  CLR,
  input  DOWN,
  input  UP,
  input  LOAD_L,
  input  C,
  input  GND,
  input  D,
  output Q_B,
  output Q_A,
  output BO_L,
  output CO_L,
  output Q_C,
  output Q_D
);

  wire and_1_out, and_2_out, and_3_out, and_4_out, and_5_out, and_6_out, and_7_out, and_8_out, and_9_out,
       and_10_out, and_11_out, and_12_out, and_13_out, and_14_out, and_15_out, and_16_out, not_1_out,
       not_2_out, not_3_out, not_4_out, not_5_out, not_6_out, not_7_out, not_8_out, not_11_out, not_12_out,
       not_13_out, not_14_out, not_15_out, not_16_out, not_17_out, not_18_out, not_19_out, or_1_out,
       or_2_out, or_3_out, or_4_out, or_5_out, or_6_out, or_7_out, or_8_out, t_ff_1_qn, t_ff_2_qn, t_ff_3_qn,
       t_ff_4_qn, undriven;

  not not_1 (not_1_out, DOWN);
  not not_2 (not_2_out, UP);
  not not_3 (not_3_out, LOAD_L);
  not not_4 (not_4_out, CLR);
  and and_1 (and_1_out, not_2_out, Q_A, undriven);
  and and_2 (and_2_out, undriven, t_ff_1_qn, not_1_out, not_3_out);
  and and_3 (and_3_out, not_2_out, Q_B, Q_A);
  and and_4 (and_4_out, t_ff_1_qn, t_ff_2_qn, not_1_out);
  and and_5 (and_5_out, not_2_out, Q_C, Q_B, Q_A);
  and and_6 (and_6_out, t_ff_1_qn, t_ff_2_qn, t_ff_3_qn, not_1_out);
  or or_1 (or_1_out, D, not_2_out, not_1_out);
  not not_5 (not_5_out, or_1_out);
  not not_6 (not_6_out, or_2_out);
  or or_2 (or_2_out, and_1_out, and_2_out);
  not not_7 (not_7_out, or_3_out);
  or or_3 (or_3_out, and_3_out, and_4_out);
  or or_4 (or_4_out, and_5_out, and_6_out);
  not not_8 (not_8_out, or_4_out);
  and and_7 (and_7_out, A, not_3_out, not_4_out);
  and and_8 (and_8_out, B, not_3_out, not_4_out);
  and and_9 (and_9_out, C, not_3_out, not_4_out);
  and and_10 (and_10_out, D, not_3_out, not_4_out);
  not not_9 (BO_L, and_11_out);
  and and_11 (and_11_out, t_ff_1_qn, t_ff_2_qn, t_ff_3_qn, t_ff_4_qn, not_1_out);
  not not_10 (CO_L, and_12_out);
  and and_12 (and_12_out, Q_A, Q_B, Q_C, Q_D, not_2_out);
  not not_11 (not_11_out, and_7_out);
  not not_12 (not_12_out, and_8_out);
  not not_13 (not_13_out, and_9_out);
  not not_14 (not_14_out, and_10_out);
  not not_15 (not_15_out, not_4_out);
  or or_5 (or_5_out, and_13_out, not_15_out);
  and and_13 (and_13_out, not_5_out, not_3_out, not_11_out, not_11_out);
  not not_16 (not_16_out, not_11_out);
  or or_6 (or_6_out, and_14_out, not_15_out);
  and and_14 (and_14_out, not_6_out, not_3_out, not_12_out, not_12_out);
  not not_17 (not_17_out, not_12_out);
  or or_7 (or_7_out, and_15_out, not_15_out);
  and and_15 (and_15_out, not_7_out, not_3_out, not_13_out, not_13_out);
  not not_18 (not_18_out, not_13_out);
  or or_8 (or_8_out, and_16_out, not_15_out);
  and and_16 (and_16_out, not_8_out, not_3_out, not_14_out, not_14_out);
  not not_19 (not_19_out, not_14_out);
  T_Flip_Flop t_ff_1 (
    .clk(not_5_out), .T(1'b1), .Q(Q_A), .Qn(t_ff_1_qn), .preset(not_16_out), .reset(or_5_out));  // open: en
  T_Flip_Flop t_ff_2 (
    .clk(not_6_out), .T(1'b1), .Q(Q_B), .Qn(t_ff_2_qn), .preset(not_17_out), .reset(or_6_out));  // open: en
  T_Flip_Flop t_ff_3 (
    .clk(not_7_out), .T(1'b1), .Q(Q_C), .Qn(t_ff_3_qn), .preset(not_18_out), .reset(or_7_out));  // open: en
  T_Flip_Flop t_ff_4 (
    .clk(not_8_out), .T(1'b1), .Q(Q_D), .Qn(t_ff_4_qn), .preset(not_19_out), .reset(or_8_out));  // open: en

  // Notes on the sheet:
  //   C: pull=up
  //   A: pull=up
  //   B: pull=up
  //   UP: pull=up
  //   D: pull=up
  //   DOWN: pull=up
  //   CLR: pull=up
endmodule

// xx540
module DIP_xx540 (
  input  OE1_L,
  input  Vcc,
  input  D0,
  input  OE2_L,
  input  D1,
  input  D2,
  input  D3,
  input  D4,
  input  D5,
  input  D6,
  input  D7,
  input  GND,
  output Q0,
  output Q1,
  output Q2,
  output Q3,
  output Q4,
  output Q5,
  output Q6,
  output Q7
);

  wire and_1_out, not_1_out, not_2_out;

  not not_1 (not_1_out, OE1_L);
  and and_1 (and_1_out, not_1_out, not_2_out);
  not not_2 (not_2_out, OE2_L);
  assign Q0 = and_1_out ? D0 : 1'bz;  // Controlled_Buffer controlled_buffer_1
  assign Q1 = and_1_out ? D1 : 1'bz;  // Controlled_Buffer controlled_buffer_2
  assign Q2 = and_1_out ? D2 : 1'bz;  // Controlled_Buffer controlled_buffer_3
  assign Q3 = and_1_out ? D3 : 1'bz;  // Controlled_Buffer controlled_buffer_4
  assign Q4 = and_1_out ? D4 : 1'bz;  // Controlled_Buffer controlled_buffer_5
  assign Q5 = and_1_out ? D5 : 1'bz;  // Controlled_Buffer controlled_buffer_6
  assign Q6 = and_1_out ? D6 : 1'bz;  // Controlled_Buffer controlled_buffer_7
  assign Q7 = and_1_out ? D7 : 1'bz;  // Controlled_Buffer controlled_buffer_8

  // Notes on the sheet:
  //   D1: pull=up
  //   D0: pull=up
  //   D3: pull=up
  //   D4: pull=up
  //   D7: pull=up
  //   D5: pull=up
  //   D6: pull=up
  //   D2: pull=up
  //   OE2_L: pull=up
  //   OE1_L: pull=up
endmodule

// xx574
module DIP_xx574 (
  input  OE_L,
  input  Vcc,
  input  D0,
  input  D1,
  input  D2,
  input  D3,
  input  D4,
  input  D5,
  input  D6,
  input  D7,
  input  GND,
  input  CP,
  output Q0,
  output Q1,
  output Q2,
  output Q3,
  output Q4,
  output Q5,
  output Q6,
  output Q7
);

  wire not_1_out;
  wire [7:0] register_1_q;

  not not_1 (not_1_out, OE_L);
  Register register_1 (.D({D7, D6, D5, D4, D3, D2, D1, D0}), .en(1'b1), .Q(register_1_q), .clk(CP), .clr(1'b0));
  assign {Q7, Q6, Q5, Q4, Q3, Q2, Q1, Q0} = not_1_out ? register_1_q : 8'bz;  // Controlled_Buffer controlled_buffer_1

  // Notes on the sheet:
  //   D6: pull=up
  //   D4: pull=up
  //   D5: pull=up
  //   D2: pull=up
  //   D3: pull=up
  //   D0: pull=up
  //   CP: pull=up
  //   OE_L: pull=up
  //   D1: pull=up
  //   D7: pull=up
endmodule

// xx02
module IC_xx02 (
  input  A1,
  input  B4,
  input  B1,
  input  A4,
  input  A2,
  input  B3,
  input  B2,
  input  A3,
  output Y1,
  output Y4,
  output Y2,
  output Y3
);

  DIP_xx02 dip_xx02_1 (
    .Y1(Y1), .A1(A1), .B1(B1), .Y2(Y2), .A2(A2), .B2(B2), .Y4(Y4), .B4(B4), .A4(A4), .Y3(Y3), .B3(B3), .A3(A3));  // open: GND, Vcc

  // Notes on the sheet:
  //   A4: pull=up
  //   B3: pull=up
  //   A1: pull=up
  //   B4: pull=up
  //   A2: pull=up
  //   B1: pull=up
endmodule

// xx04
module IC_xx04 (
  input  A1,
  input  A2,
  input  A3,
  input  A4,
  input  A5,
  input  A6,
  output Y1,
  output Y2,
  output Y3,
  output Y4,
  output Y5,
  output Y6
);

  DIP_xx04 dip_xx04_1 (
    .A1(A1), .Y1(Y1), .A2(A2), .Y2(Y2), .A3(A3), .Y3(Y3), .A6(A4), .Y6(Y4), .A5(A5), .Y5(Y5), .A4(A6), .Y4(Y6));  // open: GND, Vcc

  // Notes on the sheet:
  //   A1: pull=up
  //   A3: pull=up
  //   A6: pull=up
  //   A2: pull=up
  //   A4: pull=up
  //   A5: pull=up
endmodule

// xx08
module IC_xx08 (
  input  A1,
  input  A4,
  input  B1,
  input  B4,
  input  A2,
  input  A3,
  input  B2,
  input  B3,
  output Y1,
  output Y4,
  output Y2,
  output Y3
);

  DIP_xx08 dip_xx08_1 (
    .A1(A1), .B1(B1), .Y1(Y1), .A2(A2), .B2(B2), .Y2(Y2), .A4(A4), .B4(B4), .Y4(Y4), .A3(A3), .B3(B3), .Y3(Y3));  // open: GND, Vcc
endmodule

// xx138
module IC_xx138 (
  input  [2:0] SEL,
  input  EN1_L,
  input  EN2_L,
  input  EN3,
  output Y0_L,
  output Y1_L,
  output Y2_L,
  output Y3_L,
  output Y4_L,
  output Y5_L,
  output Y6_L,
  output Y7_L
);

  DIP_xx138 dip_xx138_1 (
    .A(SEL[2]), .B(SEL[1]), .C(SEL[0]), .EN1_L(EN1_L), .EN2_L(EN2_L), .EN3(EN3), .Y7_L(Y7_L), .Y0_L(Y0_L),
    .Y1_L(Y1_L), .Y2_L(Y2_L), .Y3_L(Y3_L), .Y4_L(Y4_L), .Y5_L(Y5_L), .Y6_L(Y6_L));  // open: GND, Vcc
endmodule

// xx139
module IC_xx139 (
  input  EN_1_L,
  input  EN_2_L,
  input  [1:0] SEL_1,
  input  [1:0] SEL_2,
  output Y10_L,
  output Y20_L,
  output Y_11_L,
  output Y21_L,
  output Y_12_L,
  output Y22_L,
  output Y_13_L,
  output Y23_L
);

  DIP_xx139 dip_xx139_1 (
    .EN1_L(EN_1_L), .A1(SEL_1[1]), .B1(SEL_1[0]), .Y10_L(Y10_L), .Y11_L(Y_11_L), .Y12_L(Y_12_L),
    .Y13_L(Y_13_L), .EN2_L(EN_2_L), .A2(SEL_2[1]), .B2(SEL_2[0]), .Y20_L(Y20_L), .Y21_L(Y21_L),
    .Y22_L(Y22_L), .Y23_L(Y23_L));  // open: GND, Vcc
endmodule

// 163
module IC_xx163 (
  input  CLR_L,
  input  CLK,
  input  [3:0] D,
  input  ENP,
  input  ENT,
  input  LOAD_L,
  output RCO,
  output [3:0] Q
);

  DIP_xx163 dip_xx163_1 (
    .CLR_L(CLR_L), .CLK(CLK), .A(D[0]), .B(D[1]), .C(D[2]), .D(D[3]), .ENP(ENP), .RCO(RCO), .Q_A(Q[0]),
    .Q_B(Q[1]), .Q_C(Q[2]), .Q_D(Q[3]), .ENT(ENT), .LOAD_L(LOAD_L));  // open: GND, Vcc
endmodule

// 169
module IC_xx169 (
  input  U_DL,
  input  [3:0] D,
  input  ENP_L,
  input  ENT_L,
  input  LOAD_L,
  input  CLK,
  output RCO_L,
  output [3:0] Q
);

  wire counter_1_carry, nor_1_out, not_1_out;

  Counter #(.width(4), .max('hf)) counter_1 (
    .load(not_1_out), .D(D), .count(nor_1_out), .Q(Q), .carry(counter_1_carry), .clk(CLK), .clr(1'b0));
  nor nor_1 (nor_1_out, ENP_L, ENT_L, CLK);
  not not_1 (not_1_out, LOAD_L);
  not not_2 (RCO_L, counter_1_carry);
endmodule

// xx174
module IC_xx174 (
  input  MR,
  input  D0,
  input  D1,
  input  D2,
  input  D3,
  input  D4,
  input  D5,
  input  CP,
  output Q0,
  output Q1,
  output Q2,
  output Q3,
  output Q4,
  output Q5
);

  DIP_xx174 dip_xx174_1 (
    .MR(MR), .Q0(Q0), .D0(D0), .D1(D1), .Q1(Q1), .D2(D2), .Q2(Q2), .Q5(Q5), .D5(D5), .D4(D4), .Q4(Q4),
    .D3(D3), .Q3(Q3), .CP(CP));  // open: GND, Vcc
endmodule

// 193
module IC_xx193 (
  input  [3:0] D,
  input  LOAD_L,
  input  CLR,
  input  DOWN,
  input  UP,
  output [3:0] Q,
  output BO_L,
  output CO_L
);

  DIP_xx193 dip_xx193_1 (
    .B(D[1]), .Q_B(Q[1]), .Q_A(Q[0]), .DOWN(DOWN), .UP(UP), .Q_C(Q[2]), .Q_D(Q[3]), .A(D[0]), .CLR(CLR),
    .BO_L(BO_L), .CO_L(CO_L), .LOAD_L(LOAD_L), .C(D[2]), .D(D[3]));  // open: GND, Vcc
endmodule

// 540
module IC_xx540 (
  input  OE1_L,
  input  OE2_L,
  input  [7:0] D,
  output [7:0] Q
);

  DIP_xx540 dip_xx540_1 (
    .OE1_L(OE1_L), .D0(D[0]), .D1(D[1]), .D2(D[2]), .D3(D[3]), .D4(D[4]), .D5(D[5]), .D6(D[6]), .D7(D[7]),
    .OE2_L(OE2_L), .Q0(Q[0]), .Q1(Q[1]), .Q2(Q[2]), .Q3(Q[3]), .Q4(Q[4]), .Q5(Q[5]), .Q6(Q[6]), .Q7(Q[7]));  // open: GND, Vcc
endmodule

// 574
module IC_xx574 (
  input  OE_L,
  input  [7:0] D,
  input  CP,
  output [7:0] O
);

  DIP_xx574 dip_xx574_1 (
    .OE_L(OE_L), .D0(D[0]), .D1(D[1]), .D2(D[2]), .D3(D[3]), .D4(D[4]), .D5(D[5]), .D6(D[6]), .D7(D[7]),
    .Q0(O[0]), .Q1(O[1]), .Q2(O[2]), .Q3(O[3]), .Q4(O[4]), .Q5(O[5]), .Q6(O[6]), .Q7(O[7]), .CP(CP));  // open: GND, Vcc

  // Notes on the sheet:
  //   CP: pull=up
  //   D: pull=up
  //   OE_L: pull=up
endmodule
